# Fritzing sketch Tempsensor (saved by Fritzing 0.9.3b)

parts:
  Part2 = Arduino Uno (Rev3)
  R1 = Resistor [tolerance=±10% resistance=330 package=THT]
  LED1 = LED - 5mm [color="Red (633nm)" package="5 mm [THT]"]
  LED7 = LED - 5mm [color="Red (633nm)" package="5 mm [THT]"]
  LED8 = LED - 5mm [color="Red (633nm)" package="5 mm [THT]"]
  LED9 = LED - 5mm [color="Red (633nm)" package="5 mm [THT]"]
  LED10 = LED - 5mm [color="Red (633nm)" package="5 mm [THT]"]
  LED11 = LED - 5mm [color="Red (633nm)" package="5 mm [THT]"]
  LED12 = LED - 5mm [color="Red (633nm)" package="5 mm [THT]"]
  LED13 = LED - 5mm [color="Red (633nm)" package="5 mm [THT]"]
  RHT1 = Humidity and Temperature Sensor RHT03
  J1 = Piezo Speaker
  R2 = Resistor [tolerance=±10% resistance=330 package=THT]
  R3 = Resistor [tolerance=±10% resistance=330 package=THT]
  R4 = Resistor [tolerance=±10% resistance=330 package=THT]
  R5 = Resistor [tolerance=±10% resistance=330 package=THT]
  R6 = Resistor [tolerance=±10% resistance=330 package=THT]
  Grove1 = Grove OLED 128x96

nets:
  N1: Part2.A4/SDA, Grove1.SDA
  N2: Part2.A5/SCL, Grove1.SCL
  N3: Part2.D8, R2.Pin_0
  N4: Part2.D9_PWM, R3.Pin_0
  N5: Part2.D10_PWM/SS, R4.Pin_0
  N6: Part2.D11_PWM/MOSI, R5.Pin_0
  N7: Part2.D12/MISO, R6.Pin_0
  GND: Part2.GND, RHT1.GND_2, Grove1.GND
  N8: Part2.D2, RHT1.Data-signal
  N9: Part2.D3_PWM, J1.pin1
  N10: Part2.D7, R1.Pin_0
  N11: Part2.3V3, J1.pin2
  VCC: Part2.5V, RHT1.Vcc, Grove1.VCC
  N12: R1.Pin_1, LED1.cathode
  N13: LED1.anode, LED7.anode, LED8.anode, LED9.anode, LED10.anode, LED11.anode, LED12.anode, LED13.anode
  N14: LED7.cathode, LED8.cathode, LED13.cathode, R6.Pin_1
  N15: LED9.cathode, R2.Pin_1
  N16: LED10.cathode, R3.Pin_1
  N17: LED11.cathode, R4.Pin_1
  N18: LED12.cathode, R5.Pin_1
